// Logisim project MAIN.circ as structural Verilog: 4 circuits, main circuit main
module main (
  input  A3,
  input  A2,
  input  A1,
  input  A0,
  input  B3,
  input  B2,
  input  B1,
  input  B0,
  output A_B,
  output A_B_2,
  output A_B_3
);

  _4_bit_comparator u_4_bit_comparator_1 (
    .A0(A0), .B0(B0), .A1(A1), .B1(B1), .A2(A2), .B2(B2), .A3(A3), .B3(B3), .A_B(A_B), .A_B_2(A_B_2),
    .A_B_3(A_B_3));

  // Notes on the sheet:
  //   Roll:2107104(Shakhoyat Rahman)
endmodule

module _1_bit_comparator (
  input  A,
  input  B,
  output A_B,
  output A_B_2,
  output A_B_3
);

  wire not_1_out, not_2_out;

  not not_1 (not_1_out, A);
  not not_2 (not_2_out, B);
  and and_1 (A_B, not_1_out, B);
  and and_2 (A_B_3, not_2_out, A);
  xnor xnor_1 (A_B_2, A_B, A_B_3);

  // Notes on the sheet:
  //   Roll : 2107104(Shakhoyat Rahman)
endmodule

module _2_bit_comparator (
  input  A0,
  input  B0,
  input  A1,
  input  B1,
  output A_B,
  output A_B_2,
  output A_B_3
);

  wire and_1_out, and_2_out, n1_bit_comparator_1_a_b, n1_bit_comparator_1_a_b_2, n1_bit_comparator_1_a_b_3,
       n1_bit_comparator_2_a_b, n1_bit_comparator_2_a_b_2, n1_bit_comparator_2_a_b_3;

  _1_bit_comparator u_1_bit_comparator_1 (
    .A(A0), .B(B0), .A_B(n1_bit_comparator_1_a_b), .A_B_2(n1_bit_comparator_1_a_b_2),
    .A_B_3(n1_bit_comparator_1_a_b_3));
  _1_bit_comparator u_1_bit_comparator_2 (
    .A(A1), .B(B1), .A_B(n1_bit_comparator_2_a_b), .A_B_2(n1_bit_comparator_2_a_b_2),
    .A_B_3(n1_bit_comparator_2_a_b_3));
  and and_1 (and_1_out, n1_bit_comparator_1_a_b, n1_bit_comparator_2_a_b_2);
  and and_2 (and_2_out, n1_bit_comparator_2_a_b_2, n1_bit_comparator_1_a_b_3);
  and and_3 (A_B_2, n1_bit_comparator_1_a_b_2, n1_bit_comparator_2_a_b_2);
  or or_1 (A_B_3, and_2_out, n1_bit_comparator_2_a_b_3);
  or or_2 (A_B, n1_bit_comparator_2_a_b, and_1_out);

  // Notes on the sheet:
  //   Roll: 2107104(Shakhoyat Rahman)
endmodule

module _4_bit_comparator (
  input  A0,
  input  B0,
  input  A1,
  input  B1,
  input  A2,
  input  B2,
  input  A3,
  input  B3,
  output A_B,
  output A_B_2,
  output A_B_3
);

  wire and_1_out, and_2_out, n2_bit_comparator_1_a_b, n2_bit_comparator_1_a_b_2, n2_bit_comparator_1_a_b_3,
       n2_bit_comparator_2_a_b, n2_bit_comparator_2_a_b_2, n2_bit_comparator_2_a_b_3;

  _2_bit_comparator u_2_bit_comparator_1 (
    .A0(A0), .B0(B0), .A1(A1), .B1(B1), .A_B(n2_bit_comparator_1_a_b), .A_B_2(n2_bit_comparator_1_a_b_2),
    .A_B_3(n2_bit_comparator_1_a_b_3));
  _2_bit_comparator u_2_bit_comparator_2 (
    .A0(A2), .B0(B2), .A1(A3), .B1(B3), .A_B(n2_bit_comparator_2_a_b), .A_B_2(n2_bit_comparator_2_a_b_2),
    .A_B_3(n2_bit_comparator_2_a_b_3));
  and and_1 (and_1_out, n2_bit_comparator_1_a_b, n2_bit_comparator_2_a_b_2);
  and and_2 (and_2_out, n2_bit_comparator_2_a_b_2, n2_bit_comparator_1_a_b_3);
  and and_3 (A_B_2, n2_bit_comparator_1_a_b_2, n2_bit_comparator_2_a_b_2);
  or or_1 (A_B, n2_bit_comparator_2_a_b, and_1_out);
  or or_2 (A_B_3, and_2_out, n2_bit_comparator_2_a_b_3);

  // Notes on the sheet:
  //   Roll:2107104(Shakhoyat Rahman)
endmodule
