// Logisim project mod6.circ as structural Verilog: 1 circuit, main circuit main
module main (
  input  Clr
);

  wire and_1_out, and_2_out, and_3_out, and_4_out, clr_out, or_1_out, or_2_out, QA_q, QA_qn, QB_q, QB_qn,
       QC_q, QC_qn;

  and and_1 (and_1_out, QA_q, QC_qn);
  and and_2 (and_2_out, QB_q, QC_q);
  and and_3 (and_3_out, QB_q, QC_qn);
  and and_4 (and_4_out, QA_qn, QB_qn, QC_q);
  or or_1 (or_1_out, and_1_out, and_2_out);
  or or_2 (or_2_out, and_3_out, and_4_out);
  D_Flip_Flop QA (.clk(clr_out), .D(or_1_out), .Q(QA_q), .Qn(QA_qn), .reset(Clr));  // open: preset, en
  D_Flip_Flop QB (.clk(clr_out), .D(or_2_out), .Q(QB_q), .Qn(QB_qn), .reset(Clr));  // open: preset, en
  D_Flip_Flop QC (.clk(clr_out), .D(QC_qn), .Q(QC_q), .Qn(QC_qn), .reset(Clr));  // open: preset, en
  Clock u_clr (.out(clr_out));
  LED QA_2 (.in(QA_q));
  LED QB_2 (.in(QB_q));
  LED QC_2 (.in(QC_q));

  // Notes on the sheet:
  //   Roll:2107104
endmodule
